// Logisim project control-logic.circ as structural Verilog: 1 circuit, main circuit control_logic
module control_logic (
  input  [31:0] Instruction,
  input  BrEq,
  input  BrLt,
  output PCSel,
  output RegWEn,
  output [2:0] ImmSel,
  output BrUn,
  output ASel,
  output BSel,
  output [3:0] ALUSel,
  output MemWEn,
  output [1:0] WBSel
);

  wire add, addi, and_1_out, and_6_out, and_8_out, and_10_out, and_12_out, and_20_out, and_21_out,
       and_22_out, and_28_out, and_30_out, and_32_out, and_34_out, and_39_out, and_40_out, and_41_out,
       and_45_out, andd, andi, auipc, beq, bge, bgeu, blt, bltu, bne, comparator_1_eq, comparator_2_eq,
       comparator_3_eq, comparator_4_eq, comparator_5_eq, comparator_6_eq, comparator_7_eq, comparator_8_eq,
       comparator_9_eq, comparator_10_eq, comparator_11_eq, comparator_12_eq, comparator_13_eq,
       comparator_14_eq, comparator_15_eq, comparator_16_eq, comparator_17_eq, comparator_18_eq,
       comparator_19_eq, comparator_20_eq, comparator_21_eq, comparator_22_eq, comparator_23_eq,
       comparator_24_eq, comparator_25_eq, comparator_26_eq, comparator_27_eq, comparator_28_eq,
       comparator_29_eq, comparator_30_eq, comparator_31_eq, comparator_32_eq, comparator_33_eq,
       comparator_34_eq, comparator_35_eq, comparator_36_eq, comparator_37_eq, comparator_38_eq,
       comparator_39_eq, comparator_40_eq, comparator_41_eq, comparator_42_eq, comparator_43_eq,
       comparator_44_eq, comparator_45_eq, comparator_46_eq, comparator_47_eq, comparator_48_eq,
       comparator_49_eq, comparator_50_eq, comparator_51_eq, comparator_52_eq, comparator_53_eq,
       comparator_54_eq, comparator_55_eq, comparator_56_eq, comparator_57_eq, comparator_58_eq,
       comparator_59_eq, comparator_60_eq, comparator_61_eq, comparator_62_eq, comparator_63_eq,
       comparator_64_eq, comparator_65_eq, comparator_66_eq, comparator_67_eq, comparator_68_eq,
       comparator_70_eq, comparator_71_eq, comparator_72_eq, comparator_73_eq, comparator_74_eq,
       comparator_75_eq, comparator_76_eq, comparator_77_eq, comparator_78_eq, comparator_79_eq,
       comparator_80_eq, comparator_81_eq, comparator_82_eq, comparator_83_eq, comparator_84_eq,
       comparator_87_eq, comparator_88_eq, comparator_89_eq, comparator_90_eq, comparator_91_eq, jal, jalr,
       lb, lh, lui, lw, mul, mulh, mulhu, multiplexer_1_out, or_1_out, ori, orr, sb, sh, slli, slll, slti,
       sltt, sraa, srai, srli, srll, sub, sw, xori, xorr;
  wire [2:0] bSel_t;
  wire [5:0] priority_encoder_1_out;
  wire [15:14] rom_1_data;

  Priority_Encoder #(.select_enc(6)) priority_encoder_1 (
    .in0(add), .in1(mul), .in2(sub), .in3(slll), .in4(mulh), .in5(mulhu), .in6(sltt), .in7(xorr), .in8(srll),
    .in9(sraa), .in10(orr), .in11(andd), .in12(lb), .in13(lh), .in14(lw), .in15(addi), .in16(slli),
    .in17(slti), .in18(xori), .in19(srli), .in20(srai), .in21(ori), .in22(andi), .in23(sb), .in24(sh),
    .in25(sw), .in26(beq), .in27(bne), .in28(blt), .in29(bge), .in30(bltu), .in31(bgeu), .in32(auipc),
    .in33(lui), .in34(jal), .in35(jalr), .out(priority_encoder_1_out));  // open: in36, in37, in38, in39, in40, in41, in42, in43, in44, in45, in46, in47, in48, in49, in50, in51, in52, in53, in54, in55, in56, in57, in58, in59, in60, in61, in62, in63, gs, en_out, en_in
  Comparator #(.width(1)) comparator_1 (.a(1'b1), .b(BrEq), .eq(comparator_1_eq));  // open: gt, lt
  Comparator #(.width(1)) comparator_2 (.a(BrEq), .b(1'b0), .eq(comparator_2_eq));  // open: gt, lt
  Comparator #(.width(1)) comparator_3 (.a(BrLt), .b(1'b1), .eq(comparator_3_eq));  // open: gt, lt
  Comparator #(.width(1)) comparator_4 (.a(BrLt), .b(1'b0), .eq(comparator_4_eq));  // open: gt, lt
  Comparator #(.width(1)) comparator_5 (.a(1'b1), .b(BrLt), .eq(comparator_5_eq));  // open: gt, lt
  Comparator #(.width(1)) comparator_6 (.a(BrLt), .b(1'b0), .eq(comparator_6_eq));  // open: gt, lt
  ROM #(.addrWidth(6), .dataWidth(16)) rom_1 (
    .addr(priority_encoder_1_out),
    .data({rom_1_data, WBSel, MemWEn, ALUSel, BSel, ASel, BrUn, ImmSel, RegWEn}));
  Multiplexer #(.select(3)) multiplexer_1 (
    .in0(comparator_1_eq), .in1(comparator_2_eq), .in2(comparator_3_eq), .in3(comparator_4_eq),
    .in4(comparator_5_eq), .in5(comparator_6_eq), .out(multiplexer_1_out), .sel(bSel_t));  // open: in6, in7
  Comparator #(.width(7)) comparator_7 (.a(Instruction[6:0]), .b(7'b1100011), .eq(comparator_7_eq));  // open: gt, lt
  Priority_Encoder priority_encoder_2 (
    .in0(beq), .in1(bne), .in2(blt), .in3(bge), .in4(bltu), .in5(bgeu), .out(bSel_t));  // open: in6, in7, en_in, gs, en_out
  and and_1 (and_1_out, multiplexer_1_out, comparator_7_eq);
  or or_1 (or_1_out, jal, jalr);
  or or_2 (PCSel, and_1_out, or_1_out);
  Comparator #(.width(7)) comparator_8 (.a(7'b0010011), .b(Instruction[6:0]), .eq(comparator_8_eq));  // open: gt, lt
  Comparator #(.width(3)) comparator_9 (.a(Instruction[14:12]), .b(3'b000), .eq(comparator_9_eq));  // open: gt, lt
  Comparator #(.width(7)) comparator_10 (.a(7'b0010011), .b(Instruction[6:0]), .eq(comparator_10_eq));  // open: gt, lt
  Comparator #(.width(3)) comparator_11 (.a(Instruction[14:12]), .b(3'b111), .eq(comparator_11_eq));  // open: gt, lt
  Comparator #(.width(7)) comparator_12 (.a(7'b0010011), .b(Instruction[6:0]), .eq(comparator_12_eq));  // open: gt, lt
  Comparator #(.width(3)) comparator_13 (.a(Instruction[14:12]), .b(3'b110), .eq(comparator_13_eq));  // open: gt, lt
  Comparator #(.width(7)) comparator_14 (.a(7'b0010011), .b(Instruction[6:0]), .eq(comparator_14_eq));  // open: gt, lt
  Comparator #(.width(3)) comparator_15 (.a(Instruction[14:12]), .b(3'b100), .eq(comparator_15_eq));  // open: gt, lt
  Comparator #(.width(7)) comparator_16 (.a(7'b0110011), .b(Instruction[6:0]), .eq(comparator_16_eq));  // open: gt, lt
  Comparator #(.width(3)) comparator_17 (.a(Instruction[14:12]), .b(3'b000), .eq(comparator_17_eq));  // open: gt, lt
  Comparator #(.width(7)) comparator_18 (.a(Instruction[31:25]), .b({7{1'b0}}), .eq(comparator_18_eq));  // open: gt, lt
  Comparator #(.width(7)) comparator_19 (.a(7'b0110011), .b(Instruction[6:0]), .eq(comparator_19_eq));  // open: gt, lt
  Comparator #(.width(3)) comparator_20 (.a(Instruction[14:12]), .b(3'b000), .eq(comparator_20_eq));  // open: gt, lt
  Comparator #(.width(7)) comparator_21 (
    .a(Instruction[31:25]), .b(7'b0100000), .eq(comparator_21_eq));  // open: gt, lt
  Comparator #(.width(7)) comparator_22 (.a(7'b0110011), .b(Instruction[6:0]), .eq(comparator_22_eq));  // open: gt, lt
  Comparator #(.width(3)) comparator_23 (.a(Instruction[14:12]), .b(3'b111), .eq(comparator_23_eq));  // open: gt, lt
  Comparator #(.width(7)) comparator_24 (.a(Instruction[31:25]), .b({7{1'b0}}), .eq(comparator_24_eq));  // open: gt, lt
  Comparator #(.width(7)) comparator_25 (.a(7'b0110011), .b(Instruction[6:0]), .eq(comparator_25_eq));  // open: gt, lt
  Comparator #(.width(3)) comparator_26 (.a(Instruction[14:12]), .b(3'b110), .eq(comparator_26_eq));  // open: gt, lt
  Comparator #(.width(7)) comparator_27 (.a(Instruction[31:25]), .b({7{1'b0}}), .eq(comparator_27_eq));  // open: gt, lt
  Comparator #(.width(7)) comparator_28 (.a(7'b1100011), .b(Instruction[6:0]), .eq(comparator_28_eq));  // open: gt, lt
  Comparator #(.width(3)) comparator_29 (.a(Instruction[14:12]), .b(3'b000), .eq(comparator_29_eq));  // open: gt, lt
  Comparator #(.width(7)) comparator_30 (.a(7'b1100011), .b(Instruction[6:0]), .eq(comparator_30_eq));  // open: gt, lt
  Comparator #(.width(3)) comparator_31 (.a(Instruction[14:12]), .b(3'b101), .eq(comparator_31_eq));  // open: gt, lt
  Comparator #(.width(7)) comparator_32 (.a(7'b1100011), .b(Instruction[6:0]), .eq(comparator_32_eq));  // open: gt, lt
  Comparator #(.width(3)) comparator_33 (.a(Instruction[14:12]), .b(3'b111), .eq(comparator_33_eq));  // open: gt, lt
  Comparator #(.width(7)) comparator_34 (.a(7'b0100011), .b(Instruction[6:0]), .eq(comparator_34_eq));  // open: gt, lt
  Comparator #(.width(3)) comparator_35 (.a(Instruction[14:12]), .b(3'b000), .eq(comparator_35_eq));  // open: gt, lt
  Comparator #(.width(7)) comparator_36 (.a(7'b0100011), .b(Instruction[6:0]), .eq(comparator_36_eq));  // open: gt, lt
  Comparator #(.width(3)) comparator_37 (.a(Instruction[14:12]), .b(3'b001), .eq(comparator_37_eq));  // open: gt, lt
  Comparator #(.width(7)) comparator_38 (.a(7'b0100011), .b(Instruction[6:0]), .eq(comparator_38_eq));  // open: gt, lt
  Comparator #(.width(3)) comparator_39 (.a(Instruction[14:12]), .b(3'b010), .eq(comparator_39_eq));  // open: gt, lt
  and and_2 (addi, comparator_8_eq, comparator_9_eq);
  and and_3 (andi, comparator_10_eq, comparator_11_eq);
  and and_4 (ori, comparator_12_eq, comparator_13_eq);
  and and_5 (xori, comparator_14_eq, comparator_15_eq);
  and and_6 (and_6_out, comparator_16_eq, comparator_17_eq);
  and and_7 (add, and_6_out, comparator_18_eq);
  and and_8 (and_8_out, comparator_19_eq, comparator_20_eq);
  and and_9 (sub, and_8_out, comparator_21_eq);
  and and_10 (and_10_out, comparator_22_eq, comparator_23_eq);
  and and_11 (andd, and_10_out, comparator_24_eq);
  and and_12 (and_12_out, comparator_25_eq, comparator_26_eq);
  and and_13 (orr, and_12_out, comparator_27_eq);
  and and_14 (beq, comparator_28_eq, comparator_29_eq);
  and and_15 (bge, comparator_30_eq, comparator_31_eq);
  and and_16 (bgeu, comparator_32_eq, comparator_33_eq);
  and and_17 (sb, comparator_34_eq, comparator_35_eq);
  and and_18 (sh, comparator_36_eq, comparator_37_eq);
  and and_19 (sw, comparator_38_eq, comparator_39_eq);
  Comparator #(.width(7)) comparator_40 (.a({7{1'b0}}), .b(Instruction[31:25]), .eq(comparator_40_eq));  // open: gt, lt
  Comparator #(.width(7)) comparator_41 (.a(7'b0010011), .b(Instruction[6:0]), .eq(comparator_41_eq));  // open: gt, lt
  Comparator #(.width(3)) comparator_42 (.a(Instruction[14:12]), .b(3'b001), .eq(comparator_42_eq));  // open: gt, lt
  Comparator #(.width(7)) comparator_43 (.a(7'b0010011), .b(Instruction[6:0]), .eq(comparator_43_eq));  // open: gt, lt
  Comparator #(.width(3)) comparator_44 (.a(Instruction[14:12]), .b(3'b101), .eq(comparator_44_eq));  // open: gt, lt
  Comparator #(.width(7)) comparator_45 (.a(7'b0010011), .b(Instruction[6:0]), .eq(comparator_45_eq));  // open: gt, lt
  Comparator #(.width(3)) comparator_46 (.a(Instruction[14:12]), .b(3'b101), .eq(comparator_46_eq));  // open: gt, lt
  Comparator #(.width(7)) comparator_47 (.a(7'b0010011), .b(Instruction[6:0]), .eq(comparator_47_eq));  // open: gt, lt
  Comparator #(.width(3)) comparator_48 (.a(Instruction[14:12]), .b(3'b010), .eq(comparator_48_eq));  // open: gt, lt
  Comparator #(.width(7)) comparator_49 (.a(7'b1100011), .b(Instruction[6:0]), .eq(comparator_49_eq));  // open: gt, lt
  Comparator #(.width(3)) comparator_50 (.a(Instruction[14:12]), .b(3'b100), .eq(comparator_50_eq));  // open: gt, lt
  Comparator #(.width(7)) comparator_51 (.a(7'b1100011), .b(Instruction[6:0]), .eq(comparator_51_eq));  // open: gt, lt
  Comparator #(.width(3)) comparator_52 (.a(Instruction[14:12]), .b(3'b110), .eq(comparator_52_eq));  // open: gt, lt
  Comparator #(.width(7)) comparator_53 (.a(7'b1100011), .b(Instruction[6:0]), .eq(comparator_53_eq));  // open: gt, lt
  Comparator #(.width(3)) comparator_54 (.a(Instruction[14:12]), .b(3'b001), .eq(comparator_54_eq));  // open: gt, lt
  Comparator #(.width(7)) comparator_55 (.a(7'b1100111), .b(Instruction[6:0]), .eq(comparator_55_eq));  // open: gt, lt
  Comparator #(.width(3)) comparator_56 (.a(Instruction[14:12]), .b(3'b000), .eq(comparator_56_eq));  // open: gt, lt
  and and_20 (and_20_out, comparator_41_eq, comparator_42_eq);
  and and_21 (and_21_out, comparator_43_eq, comparator_44_eq);
  and and_22 (and_22_out, comparator_45_eq, comparator_46_eq);
  and and_23 (slti, comparator_47_eq, comparator_48_eq);
  Comparator #(.width(7)) comparator_57 (.a(7'b0110011), .b(Instruction[6:0]), .eq(comparator_57_eq));  // open: gt, lt
  Comparator #(.width(3)) comparator_58 (.a(Instruction[14:12]), .b(3'b100), .eq(comparator_58_eq));  // open: gt, lt
  Comparator #(.width(7)) comparator_59 (.a(Instruction[31:25]), .b({7{1'b0}}), .eq(comparator_59_eq));  // open: gt, lt
  Comparator #(.width(7)) comparator_60 (.a(7'b0110011), .b(Instruction[6:0]), .eq(comparator_60_eq));  // open: gt, lt
  Comparator #(.width(3)) comparator_61 (.a(Instruction[14:12]), .b(3'b001), .eq(comparator_61_eq));  // open: gt, lt
  Comparator #(.width(7)) comparator_62 (.a(Instruction[31:25]), .b({7{1'b0}}), .eq(comparator_62_eq));  // open: gt, lt
  Comparator #(.width(7)) comparator_63 (.a(7'b0110011), .b(Instruction[6:0]), .eq(comparator_63_eq));  // open: gt, lt
  Comparator #(.width(3)) comparator_64 (.a(Instruction[14:12]), .b(3'b101), .eq(comparator_64_eq));  // open: gt, lt
  Comparator #(.width(7)) comparator_65 (.a(Instruction[31:25]), .b({7{1'b0}}), .eq(comparator_65_eq));  // open: gt, lt
  Comparator #(.width(7)) comparator_66 (.a(7'b0110011), .b(Instruction[6:0]), .eq(comparator_66_eq));  // open: gt, lt
  Comparator #(.width(3)) comparator_67 (.a(Instruction[14:12]), .b(3'b101), .eq(comparator_67_eq));  // open: gt, lt
  Comparator #(.width(7)) comparator_68 (
    .a(Instruction[31:25]), .b(7'b0100000), .eq(comparator_68_eq));  // open: gt, lt
  and and_24 (blt, comparator_49_eq, comparator_50_eq);
  and and_25 (bltu, comparator_51_eq, comparator_52_eq);
  and and_26 (bne, comparator_53_eq, comparator_54_eq);
  Comparator #(.width(7)) comparator_69 (.a(7'b0010111), .b(Instruction[6:0]), .eq(auipc));  // open: gt, lt
  and and_27 (slli, comparator_40_eq, and_20_out);
  Comparator #(.width(7)) comparator_70 (.a({7{1'b0}}), .b(Instruction[31:25]), .eq(comparator_70_eq));  // open: gt, lt
  Comparator #(.width(7)) comparator_71 (
    .a(7'b0100000), .b(Instruction[31:25]), .eq(comparator_71_eq));  // open: gt, lt
  and and_28 (and_28_out, comparator_57_eq, comparator_58_eq);
  and and_29 (xorr, and_28_out, comparator_59_eq);
  and and_30 (and_30_out, comparator_60_eq, comparator_61_eq);
  and and_31 (slll, and_30_out, comparator_62_eq);
  and and_32 (and_32_out, comparator_63_eq, comparator_64_eq);
  and and_33 (srll, and_32_out, comparator_65_eq);
  and and_34 (and_34_out, comparator_66_eq, comparator_67_eq);
  and and_35 (sraa, and_34_out, comparator_68_eq);
  and and_36 (jalr, comparator_55_eq, comparator_56_eq);
  and and_37 (srli, comparator_70_eq, and_21_out);
  and and_38 (srai, comparator_71_eq, and_22_out);
  Comparator #(.width(7)) comparator_72 (.a(7'b0110011), .b(Instruction[6:0]), .eq(comparator_72_eq));  // open: gt, lt
  Comparator #(.width(3)) comparator_73 (.a(Instruction[14:12]), .b(3'b010), .eq(comparator_73_eq));  // open: gt, lt
  Comparator #(.width(7)) comparator_74 (.a(Instruction[31:25]), .b({7{1'b0}}), .eq(comparator_74_eq));  // open: gt, lt
  Comparator #(.width(7)) comparator_75 (.a(7'b0110011), .b(Instruction[6:0]), .eq(comparator_75_eq));  // open: gt, lt
  Comparator #(.width(3)) comparator_76 (.a(Instruction[14:12]), .b(3'b000), .eq(comparator_76_eq));  // open: gt, lt
  Comparator #(.width(7)) comparator_77 (
    .a(Instruction[31:25]), .b(7'b0000001), .eq(comparator_77_eq));  // open: gt, lt
  Comparator #(.width(7)) comparator_78 (.a(7'b0110011), .b(Instruction[6:0]), .eq(comparator_78_eq));  // open: gt, lt
  Comparator #(.width(3)) comparator_79 (.a(Instruction[14:12]), .b(3'b001), .eq(comparator_79_eq));  // open: gt, lt
  Comparator #(.width(7)) comparator_80 (
    .a(Instruction[31:25]), .b(7'b0000001), .eq(comparator_80_eq));  // open: gt, lt
  Comparator #(.width(7)) comparator_81 (.a(7'b0000011), .b(Instruction[6:0]), .eq(comparator_81_eq));  // open: gt, lt
  Comparator #(.width(3)) comparator_82 (.a(Instruction[14:12]), .b(3'b000), .eq(comparator_82_eq));  // open: gt, lt
  Comparator #(.width(7)) comparator_83 (.a(7'b0000011), .b(Instruction[6:0]), .eq(comparator_83_eq));  // open: gt, lt
  Comparator #(.width(3)) comparator_84 (.a(Instruction[14:12]), .b(3'b001), .eq(comparator_84_eq));  // open: gt, lt
  Comparator #(.width(7)) comparator_85 (.a(7'b0110111), .b(Instruction[6:0]), .eq(lui));  // open: gt, lt
  Comparator #(.width(7)) comparator_86 (.a(7'b1101111), .b(Instruction[6:0]), .eq(jal));  // open: gt, lt
  and and_39 (and_39_out, comparator_72_eq, comparator_73_eq);
  and and_40 (and_40_out, comparator_75_eq, comparator_76_eq);
  and and_41 (and_41_out, comparator_78_eq, comparator_79_eq);
  Comparator #(.width(7)) comparator_87 (.a(7'b0110011), .b(Instruction[6:0]), .eq(comparator_87_eq));  // open: gt, lt
  Comparator #(.width(3)) comparator_88 (.a(Instruction[14:12]), .b(3'b011), .eq(comparator_88_eq));  // open: gt, lt
  Comparator #(.width(7)) comparator_89 (
    .a(Instruction[31:25]), .b(7'b0000001), .eq(comparator_89_eq));  // open: gt, lt
  Comparator #(.width(7)) comparator_90 (.a(7'b0000011), .b(Instruction[6:0]), .eq(comparator_90_eq));  // open: gt, lt
  Comparator #(.width(3)) comparator_91 (.a(Instruction[14:12]), .b(3'b010), .eq(comparator_91_eq));  // open: gt, lt
  and and_42 (sltt, and_39_out, comparator_74_eq);
  and and_43 (mul, and_40_out, comparator_77_eq);
  and and_44 (mulh, and_41_out, comparator_80_eq);
  and and_45 (and_45_out, comparator_87_eq, comparator_88_eq);
  and and_46 (mulhu, and_45_out, comparator_89_eq);
  and and_47 (lb, comparator_81_eq, comparator_82_eq);
  and and_48 (lh, comparator_83_eq, comparator_84_eq);
  and and_49 (lw, comparator_90_eq, comparator_91_eq);

  // Other names for the same wires on the sheet: opcode[6:0] = Instruction[6:0]; funct3[2:0] = Instruction[14:12];
  //   funct7[6:0] = Instruction[31:25]

  // Notes on the sheet:
  //   INPUTS to your circuit
  //   contents of rom_1 (hex, n*v repeats v):
  //   1001 1401 1601 1081 1481 1581 1101 1201 1281 1681 1301 1001 41 41 41 1041 10c1 1141 1241 12c1 16c1
  //   1341 13c1 842 842 842 4*64 74 74 1067 17c7 2069 2041
  //   ROM FOR CONTROL LOGIC
  //   DON'T CHANGE THE LOCATIONS OF THE INPUTS AND OUTPUTS!
  //   This is only if you choose to do the ROM option
  //   CONNECT
  //   WIRE
  //   TO
  //   USE
  //   ROM
  //   OUTPUT from your circuit
  //   Reminder: If using ROM, use combinational logic for PCSel
endmodule
