// Logisim project cpu.circ as structural Verilog: 1 circuit, main circuit cpu
module cpu (
  input  clk,
  input  [31:0] Instruction,
  input  [31:0] MemReadData,
  output [31:0] MemAddress,
  output [31:0] ProgramCounter,
  output [31:0] ra,
  output [31:0] sp,
  output [31:0] t0,
  output [31:0] t1,
  output [31:0] t2,
  output [31:0] s0,
  output [31:0] s1,
  output [31:0] a0,
  output [3:0] MemWriteMask,
  output [31:0] MemWriteData
);

  wire ASel, BrEq, BrLt, BrUn, BSel, MemWEn, PCSel, RegWEn;
  wire [1:0] WBSel;
  wire [2:0] funct3, ImmSel;
  wire [3:0] ALUSel;
  wire [6:0] imm;
  wire [24:0] InstructionStage2;
  wire [31:0] A_Val, B_Val, Immediate, loaded, multiplexer_1_out, multiplexer_2_out, PCplusFourStage1,
       PCplusFourStage2, ProgramCounterStage2, ReadData1, ReadData2, WriteData;

  Register #(.width(32)) register_1 (.D(PCplusFourStage1), .clk(clk), .Q(PCplusFourStage2));  // open: en, clr
  Adder #(.width(32)) adder_1 (.a(ProgramCounter), .b(32'h4), .out(PCplusFourStage1));  // open: cin, cout
  Multiplexer #(.width(32)) multiplexer_1 (
    .in0(PCplusFourStage1), .in1(MemAddress), .out(multiplexer_1_out), .sel(PCSel));
  Multiplexer #(.width(32)) multiplexer_2 (.in0(Instruction), .in1(32'h13), .out(multiplexer_2_out), .sel(PCSel));
  Register #(.width(32)) PCstage1 (.D(multiplexer_1_out), .clk(clk), .Q(ProgramCounter));  // open: en, clr
  Register #(.width(32)) PCstage2 (.D(ProgramCounter), .clk(clk), .Q(ProgramCounterStage2));  // open: en, clr
  Register #(.width(32)) InstructionFetch (
    .D(multiplexer_2_out), .clk(clk), .Q({imm, InstructionStage2[24:15], funct3, InstructionStage2[11:0]}));  // open: en, clr
  control_logic control_logic_1 (
    .Instruction({imm, InstructionStage2[24:15], funct3, InstructionStage2[11:0]}), .BrEq(BrEq), .BrLt(BrLt),
    .PCSel(PCSel), .RegWEn(RegWEn), .ImmSel(ImmSel), .BrUn(BrUn), .ASel(ASel), .BSel(BSel), .ALUSel(ALUSel),
    .MemWEn(MemWEn), .WBSel(WBSel));
  Multiplexer #(.width(32)) multiplexer_3 (.in0(ReadData1), .in1(ProgramCounterStage2), .out(A_Val), .sel(ASel));
  regfile regfile_1 (
    .ReadIndex1(InstructionStage2[19:15]), .ReadIndex2(InstructionStage2[24:20]),
    .WriteIndex(InstructionStage2[11:7]), .WriteData(WriteData), .RegWEn(RegWEn), .clk(clk), .ra(ra),
    .sp(sp), .t0(t0), .t1(t1), .t2(t2), .s0(s0), .s1(s1), .a0(a0), .ReadData1(ReadData1),
    .ReadData2(ReadData2));
  imm_gen imm_gen_1 (
    .Instruction({imm, InstructionStage2[24:15], funct3, InstructionStage2[11:0]}), .ImmSel(ImmSel),
    .Immediate(Immediate));
  Multiplexer #(.width(32)) multiplexer_4 (.in0(ReadData2), .in1(Immediate), .out(B_Val), .sel(BSel));
  alu alu_1 (.A(A_Val), .B(B_Val), .ALUSel(ALUSel), .ALUResult(MemAddress));
  branch_comp branch_comp_1 (.BrData1(ReadData1), .BrData2(ReadData2), .BrUn(BrUn), .BrEq(BrEq), .BrLt(BrLt));
  Multiplexer #(.select(2), .width(32)) multiplexer_5 (
    .in0(loaded), .in1(MemAddress), .in2(PCplusFourStage2), .out(WriteData), .sel(WBSel));  // open: in3
  partial_store partial_store_1 (
    .Instruction({imm, InstructionStage2[24:15], funct3, InstructionStage2[11:0]}), .MemAddress(MemAddress),
    .DataFromReg(ReadData2), .MemWEn(MemWEn), .MemWriteMask(MemWriteMask), .DataToMem(MemWriteData));
  partial_load partial_load_1 (
    .Instruction({imm, InstructionStage2[24:15], funct3, InstructionStage2[11:0]}), .MemAddress(MemAddress),
    .DataFromMem(MemReadData), .DataToReg(loaded));

  // Other names for the same wires on the sheet: InstructionStage1[31:0] = Instruction;
  //   opcode[6:0] = InstructionStage2[6:0]; rd[4:0] = InstructionStage2[11:7];
  //   InstructionStage2 (some bits) = {imm, funct3}; rs1[4:0] = InstructionStage2[19:15];
  //   rs2[4:0] = InstructionStage2[24:20]; ProgramCounterStage1[31:0] = ProgramCounter; ALUResult[31:0] = MemAddress;
  //   WBInput[31:0] = MemAddress

  // Notes on the sheet:
  //   To IMEM
  //   IMEM (do **NOT** move this)
  //   From IMEM
  //   Inputs/Outputs for testing. Do **NOT** move these.
  //   It is OK to move the PC, RegFile, ALU, MEM, Branch Comp, Imm Gen, Partial Load, Partial Store and Control Logic to wherever is most convenient for you when constructing your CPU, and to delete this text
  //   To DMEM
  //   DMEM (do **NOT** move this)
  //   From DMEM
endmodule
