// Logisim project regfile.circ as structural Verilog: 1 circuit, main circuit regfile
module regfile (
  input  [4:0] ReadIndex1,
  input  [4:0] ReadIndex2,
  input  [4:0] WriteIndex,
  input  [31:0] WriteData,
  input  RegWEn,
  input  clk,
  output [31:0] ra,
  output [31:0] sp,
  output [31:0] t0,
  output [31:0] t1,
  output [31:0] t2,
  output [31:0] s0,
  output [31:0] s1,
  output [31:0] a0,
  output [31:0] ReadData1,
  output [31:0] ReadData2
);

  wire e1, e2, e3, e4, e5, e6, e7, e8, e9, e10, e11, e12, e13, e14, e15, e16, e17, e18, e19, e20, e21, e22,
       e23, e24, e25, e26, e27, e28, e29, e30, e31, e32, x1, x2, x3, x4, x5, x6, x7, x8, x9, x10, x11, x12,
       x13, x14, x15, x16, x17, x18, x19, x20, x21, x22, x23, x24, x25, x26, x27, x28, x29, x30, x31, x32;
  wire [31:0] o1, o4, o5, o12, o13, o14, o15, o16, o17, o18, o19, o20, o21, o22, o23, o24, o25, o26, o27,
       o28, o29, o30, o31, o32;

  Register #(.width(32)) register_1 (.D({32{1'b0}}), .en(e1), .clk(clk), .Q(o1));  // open: clr
  Register #(.width(32)) register_2 (.D(WriteData), .en(e2), .clk(clk), .Q(ra));  // open: clr
  Register #(.width(32)) register_3 (.D(WriteData), .en(e3), .clk(clk), .Q(sp));  // open: clr
  Register #(.width(32)) register_4 (.D(WriteData), .en(e4), .clk(clk), .Q(o4));  // open: clr
  Register #(.width(32)) register_5 (.D(WriteData), .en(e5), .clk(clk), .Q(o5));  // open: clr
  Register #(.width(32)) register_6 (.D(WriteData), .en(e6), .clk(clk), .Q(t0));  // open: clr
  Register #(.width(32)) register_7 (.D(WriteData), .en(e7), .clk(clk), .Q(t1));  // open: clr
  Register #(.width(32)) register_8 (.D(WriteData), .en(e8), .clk(clk), .Q(t2));  // open: clr
  Register #(.width(32)) register_9 (.D(WriteData), .en(e9), .clk(clk), .Q(s0));  // open: clr
  Register #(.width(32)) register_10 (.D(WriteData), .en(e10), .clk(clk), .Q(s1));  // open: clr
  Register #(.width(32)) register_11 (.D(WriteData), .en(e11), .clk(clk), .Q(a0));  // open: clr
  Register #(.width(32)) register_12 (.D(WriteData), .en(e12), .clk(clk), .Q(o12));  // open: clr
  Register #(.width(32)) register_13 (.D(WriteData), .en(e13), .clk(clk), .Q(o13));  // open: clr
  Register #(.width(32)) register_14 (.D(WriteData), .en(e14), .clk(clk), .Q(o14));  // open: clr
  Register #(.width(32)) register_15 (.D(WriteData), .en(e15), .clk(clk), .Q(o15));  // open: clr
  Register #(.width(32)) register_16 (.D(WriteData), .en(e16), .clk(clk), .Q(o16));  // open: clr
  Decoder #(.select(5)) decoder_1 (
    .out0(x1), .out1(x2), .out2(x3), .out3(x4), .out4(x5), .out5(x6), .out6(x7), .out7(x8), .out8(x9),
    .out9(x10), .out10(x11), .out11(x12), .out12(x13), .out13(x14), .out14(x15), .out15(x16), .out16(x17),
    .out17(x18), .out18(x19), .out19(x20), .out20(x21), .out21(x22), .out22(x23), .out23(x24), .out24(x25),
    .out25(x26), .out26(x27), .out27(x28), .out28(x29), .out29(x30), .out30(x31), .out31(x32),
    .sel(WriteIndex));  // open: en
  Register #(.width(32)) register_17 (.D(WriteData), .en(e17), .clk(clk), .Q(o17));  // open: clr
  Register #(.width(32)) register_18 (.D(WriteData), .en(e18), .clk(clk), .Q(o18));  // open: clr
  Register #(.width(32)) register_19 (.D(WriteData), .en(e19), .clk(clk), .Q(o19));  // open: clr
  Register #(.width(32)) register_20 (.D(WriteData), .en(e20), .clk(clk), .Q(o20));  // open: clr
  Register #(.width(32)) register_21 (.D(WriteData), .en(e21), .clk(clk), .Q(o21));  // open: clr
  Register #(.width(32)) register_22 (.D(WriteData), .en(e22), .clk(clk), .Q(o22));  // open: clr
  Register #(.width(32)) register_23 (.D(WriteData), .en(e23), .clk(clk), .Q(o23));  // open: clr
  Register #(.width(32)) register_24 (.D(WriteData), .en(e24), .clk(clk), .Q(o24));  // open: clr
  and and_1 (e1, x1, RegWEn);
  and and_2 (e2, x2, RegWEn);
  and and_3 (e3, x3, RegWEn);
  and and_4 (e4, x4, RegWEn);
  and and_5 (e5, x5, RegWEn);
  and and_6 (e6, x6, RegWEn);
  and and_7 (e7, x7, RegWEn);
  and and_8 (e8, x8, RegWEn);
  and and_9 (e9, x9, RegWEn);
  and and_10 (e10, x10, RegWEn);
  and and_11 (e11, x11, RegWEn);
  and and_12 (e12, x12, RegWEn);
  and and_13 (e13, x13, RegWEn);
  and and_14 (e14, x14, RegWEn);
  and and_15 (e15, x15, RegWEn);
  and and_16 (e16, x16, RegWEn);
  and and_17 (e17, x17, RegWEn);
  and and_18 (e18, x18, RegWEn);
  and and_19 (e19, x19, RegWEn);
  and and_20 (e20, x20, RegWEn);
  Register #(.width(32)) register_25 (.D(WriteData), .en(e25), .clk(clk), .Q(o25));  // open: clr
  Register #(.width(32)) register_26 (.D(WriteData), .en(e26), .clk(clk), .Q(o26));  // open: clr
  Register #(.width(32)) register_27 (.D(WriteData), .en(e27), .clk(clk), .Q(o27));  // open: clr
  Register #(.width(32)) register_28 (.D(WriteData), .en(e28), .clk(clk), .Q(o28));  // open: clr
  Register #(.width(32)) register_29 (.D(WriteData), .en(e29), .clk(clk), .Q(o29));  // open: clr
  Register #(.width(32)) register_30 (.D(WriteData), .en(e30), .clk(clk), .Q(o30));  // open: clr
  Register #(.width(32)) register_31 (.D(WriteData), .en(e31), .clk(clk), .Q(o31));  // open: clr
  Register #(.width(32)) register_32 (.D(WriteData), .en(e32), .clk(clk), .Q(o32));  // open: clr
  and and_21 (e21, x21, RegWEn);
  and and_22 (e22, x22, RegWEn);
  and and_23 (e23, x23, RegWEn);
  and and_24 (e24, x24, RegWEn);
  and and_25 (e25, x25, RegWEn);
  and and_26 (e26, x26, RegWEn);
  and and_27 (e27, x27, RegWEn);
  and and_28 (e28, x28, RegWEn);
  and and_29 (e29, x29, RegWEn);
  and and_30 (e30, x30, RegWEn);
  and and_31 (e31, x31, RegWEn);
  and and_32 (e32, x32, RegWEn);
  Multiplexer #(.select(5), .width(32)) multiplexer_1 (
    .in0(o1), .in1(ra), .in2(sp), .in3(o4), .in4(o5), .in5(t0), .in6(t1), .in7(t2), .in8(s0), .in9(s1),
    .in10(a0), .in11(o12), .in12(o13), .in13(o14), .in14(o15), .in15(o16), .in16(o17), .in17(o18),
    .in18(o19), .in19(o20), .in20(o21), .in21(o22), .in22(o23), .in23(o24), .in24(o25), .in25(o26),
    .in26(o27), .in27(o28), .in28(o29), .in29(o30), .in30(o31), .in31(o32), .out(ReadData1), .sel(ReadIndex1));
  Multiplexer #(.select(5), .width(32)) multiplexer_2 (
    .in0(o1), .in1(ra), .in2(sp), .in3(o4), .in4(o5), .in5(t0), .in6(t1), .in7(t2), .in8(s0), .in9(s1),
    .in10(a0), .in11(o12), .in12(o13), .in13(o14), .in14(o15), .in15(o16), .in16(o17), .in17(o18),
    .in18(o19), .in19(o20), .in20(o21), .in21(o22), .in22(o23), .in23(o24), .in24(o25), .in25(o26),
    .in26(o27), .in27(o28), .in28(o29), .in29(o30), .in30(o31), .in31(o32), .out(ReadData2), .sel(ReadIndex2));

  // Other names for the same wires on the sheet: o2[31:0] = ra; o3[31:0] = sp; o6[31:0] = t0; o7[31:0] = t1;
  //   o8[31:0] = t2; o9[31:0] = s0; o10[31:0] = s1; o11[31:0] = a0

  // Notes on the sheet:
  //   INPUTS to your circuit
  //   DON'T CHANGE THE LOCATIONS OF THE INPUTS AND OUTPUTS!
  //   These are DEBUG/TEST outputs from your circuit.
  //   OUTPUTS from your circuit
endmodule
